// Logisim project prelab-a.circ as structural Verilog: 1 circuit, main circuit main
module main (
  input  in_1,
  input  in_2,
  input  in_3,
  input  in_4,
  input  A,
  input  B,
  input  C,
  input  D,
  output out_9,
  output out_10,
  output F
);

  wire and_1_out, and_2_out, and_3_out, and_4_out, and_5_out, and_6_out, and_7_out, and_8_out, and_9_out,
       and_10_out, and_11_out, and_12_out, and_13_out, and_14_out, and_15_out, not_1_out, not_2_out,
       not_3_out, not_4_out, not_5_out, not_6_out, not_7_out, not_8_out, not_9_out, not_10_out, not_13_out,
       not_14_out;

  and and_1 (and_1_out, in_3, in_3);
  and and_2 (and_2_out, in_4, in_4);
  and and_3 (and_3_out, A, B);
  and and_4 (and_4_out, A, B);
  and and_5 (and_5_out, C, D);
  and and_6 (and_6_out, C, D);
  not not_1 (not_1_out, and_7_out);
  and and_7 (and_7_out, in_1, in_2);
  and and_8 (and_8_out, in_2, in_1);
  not not_2 (not_2_out, and_8_out);
  not not_3 (not_3_out, and_1_out);
  not not_4 (not_4_out, and_2_out);
  not not_5 (not_5_out, and_3_out);
  and and_9 (and_9_out, not_5_out, not_6_out);
  not not_6 (not_6_out, and_4_out);
  not not_7 (not_7_out, and_5_out);
  and and_10 (and_10_out, not_7_out, not_8_out);
  not not_8 (not_8_out, and_6_out);
  and and_11 (and_11_out, not_1_out, not_2_out);
  and and_12 (and_12_out, not_3_out, not_4_out);
  not not_9 (not_9_out, and_9_out);
  not not_10 (not_10_out, and_10_out);
  not not_11 (out_9, and_11_out);
  not not_12 (out_10, and_12_out);
  not not_13 (not_13_out, and_13_out);
  and and_13 (and_13_out, not_9_out, not_9_out);
  and and_14 (and_14_out, not_10_out, not_10_out);
  not not_14 (not_14_out, and_14_out);
  and and_15 (and_15_out, not_13_out, not_14_out);
  not not_15 (F, and_15_out);

  // Notes on the sheet:
  //   OR WITH NAND GATES
  //   AND WITH NAND GATES
  //   F=AB+CD
endmodule
