# Fritzing sketch deskinator-wiring (saved by Fritzing 1.0.5)
breadboards: 3

parts:
  Part1 = Adafruit BNO085 9-DOF Orientation IMU Fusion [part_number="Addfruit #4754"]
  M1 = Stepper Motor - Bipolar
  M2 = Stepper Motor - Bipolar
  Mod2 = Raspberry Pi 4B
  Part2 = Adafruit APDS9960 Proximity Sensor [part_number="Adafruit #3595"]
  U1 = 4S Li-ion/LiPo 14.8 V XT60 [package=lipo-2000]
  M4 = DC Vacuum Fan 12V
  S1 = Toggle Switch [package=THT]
  F1 = FUSE [package=fuse_5mm]
  XL4016-12V = DC_DC_XL4016 [package=board_screw]
  XL4015-5_1V = DC_DC_XL4015 [package=board_screw]
  Mod3 = TMC2209 [package=THT]
  Mod4 = TMC2209 [package=THT]
  Part11 = Adafruit TCA9548A
  Part12 = Adafruit APDS9960 Proximity Sensor [part_number="Adafruit #3595"]
  Part13 = Adafruit APDS9960 Proximity Sensor [part_number="Adafruit #3595"]
  Part14 = Adafruit APDS9960 Proximity Sensor [part_number="Adafruit #3595"]
  Part15 = Adafruit APDS9960 Proximity Sensor [part_number="Adafruit #3595"]
  Part16 = Adafruit APDS9960 Proximity Sensor [part_number="Adafruit #3595"]
  Part17 = Adafruit APDS9960 Proximity Sensor [part_number="Adafruit #3595"]
  Part18 = Adafruit APDS9960 Proximity Sensor [part_number="Adafruit #3595"]
  Part19 = Adafruit APDS9960 Proximity Sensor [part_number="Adafruit #3595"]
  Passive_Buzzer = Passive Buzzer
  Q1 = NPN-Transistor [package="TO92 [THT]"]
  R3 = 10kΩ Resistor [package="0402 [SMD]"]

nets:
  VCC: Part1.VCC, Mod2.3V3, Part2.VCC, Mod3.VIO, Mod4.VIO, Part11.VCC, Part12.VCC, Part13.VCC, Part14.VCC, Part15.VCC, Part16.VCC, Part17.VCC, Part18.VCC, Part19.VCC
  GND: Part1.GND, Mod2.GND, Part2.GND, U1.-, S1.L2, XL4016-12V.IN+, XL4016-12V.IN-, XL4015-5_1V.IN+, XL4015-5_1V.IN-, XL4015-5_1V.OUT-, Mod3.GND, Mod3.VM, Mod4.GND, Mod4.VM, Part11.GND, Part12.GND, Part13.GND, Part14.GND, Part15.GND, Part16.GND, Part17.GND, Part18.GND, Part19.GND, Passive_Buzzer.-, Q1.E
  N1: Part1.SCL/SCK/RX, Mod2.GPIO14
  N2: Part1.SDA/MISO/TX, Mod2.GPIO15
  N3: M1.A, Mod3.M1B
  N4: M1.C, Mod3.M1A
  N5: M1.B, Mod3.M2A
  N6: M1.D, Mod3.M2B
  N7: M2.A, Mod4.M1B
  N8: M2.C, Mod4.M1A
  N9: M2.B, Mod4.M2A
  N10: M2.D, Mod4.M2B
  N11: Mod2.5V, XL4015-5_1V.OUT+
  N12: Mod2.GPIO2, Part11.INPUTSDA
  N13: Mod2.GPIO3, Part11.INPUTSCL
  N14: Mod2.GPIO4, Part19.SCL
  N15: Mod2.GPIO17, Part19.SDA
  N16: Mod2.GPIO22, Mod4.Step
  N17: Mod2.GPIO23, Mod4.Dir
  N18: Mod2.GPIO24, R3.Pin_1
  N19: Mod2.GPIO16, Mod3.EN, Mod4.EN
  N20: Mod2.GPIO20, Mod3.Step
  N21: Mod2.GPIO21, Mod3.Dir
  N22: Part2.SCL, Part11.0SCL
  N23: Part2.SDA, Part11.0SDA
  N24: U1.+, F1.2
  N25: M4.pin_1, XL4016-12V.OUT+
  N26: M4.pin_2, XL4016-12V.OUT-
  N27: S1.L1, F1.1
  N28: Part11.2SDA, Part13.SDA
  N29: Part11.2SCL, Part13.SCL
  N30: Part11.3SDA, Part14.SDA
  N31: Part11.3SCL, Part14.SCL
  N32: Part11.4SDA, Part17.SDA
  N33: Part11.4SCL, Part17.SCL
  N34: Part11.5SDA, Part18.SDA
  N35: Part11.5SCL, Part18.SCL
  N36: Part11.6SDA, Part16.SDA
  N37: Part11.6SCL, Part16.SCL
  N38: Part11.7SDA, Part15.SDA
  N39: Part11.7SCL, Part15.SCL
  N40: Part11.1SDA, Part12.SDA
  N41: Part11.1SCL, Part12.SCL
  N42: Passive_Buzzer.S, Q1.C
  N43: Q1.B, R3.Pin_0

notes:
  12V
  5.10V

custom parts:
  Adafruit APDS9960 Proximity Sensor: This breakout is chock full o' sensors! Add basic gesture sensing, RGB color sensing, proximity sensing, or ambient light sensing to your project with the Adafruit APDS9960 Proximity, Light, RGB and Gesture Sensor. When connected to your microcontroller (running our library code) it can detect simple gestures (left to right, right to left, up to down, down to up are currently supported),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
  4S Li-ion/LiPo 14.8 V XT60: 4S Li-ion/LiPo pack, 14.8 V nominal (16.8 V full), XT60 connector.
  DC Vacuum Fan 12V: DC Vacuum Fan
  DC_DC_XL4015: DC-DC Converter step down voltage regulator XL4016 custom sketch.
  TMC2209: TMC2209-LA stepper motor controller and driver. Supply voltage 4.75-28V Iphase up to 1.77A rms (2.5A peak)
  Adafruit TCA9548A: You just found the perfect I2C sensor, and you want to wire up two or three or more of them to your Arduino when you realize "Uh oh, this chip has a fixed I2C address, and from what I know about I2C, you cannot have two devices with the same address on the same SDA/SCL pins!" Are you out of luck? You would be, if you didn't have this ultra-cool TCA9548A 1-to-8 I2C multiplexer! Finally, a way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
  10kΩ Resistor: Resistor Basic schematic elements and footprints for 0603, 1206, and PTH resistors.
